// Logisim project 4bitcounter.circ as structural Verilog: 1 circuit, main circuit 4bitcounter
module _4bitcounter (
);

  wire and_1_out, and_2_out, and_3_out, and_4_out, and_5_out, and_6_out, b1, b2, b3, b4, clock_1_out,
       not_1_out, not_2_out, rst_out, xor_1_out, xor_2_out, xor_3_out;

  Clock clock_1 (.out(clock_1_out));
  Button rst (.out(rst_out));
  and and_1 (and_1_out, b1, b2);
  not not_1 (not_1_out, rst_out);
  not not_2 (not_2_out, b1);
  xor xor_1 (xor_1_out, b1, b2);
  xor xor_2 (xor_2_out, and_1_out, b3);
  and and_2 (and_2_out, and_1_out, b3);
  xor xor_3 (xor_3_out, and_2_out, b4);
  and and_3 (and_3_out, not_2_out, 1'b1, not_1_out);
  and and_4 (and_4_out, xor_1_out, 1'b1, not_1_out);
  and and_5 (and_5_out, xor_2_out, 1'b1, not_1_out);
  and and_6 (and_6_out, xor_3_out, 1'b1, not_1_out);
  D_Flip_Flop d_ff_1 (.clk(clock_1_out), .D(and_3_out), .Q(b1));  // open: Qn, preset, en, reset
  D_Flip_Flop d_ff_2 (.clk(clock_1_out), .D(and_4_out), .Q(b2));  // open: Qn, preset, en, reset
  D_Flip_Flop d_ff_3 (.clk(clock_1_out), .D(and_5_out), .Q(b3));  // open: Qn, preset, en, reset
  D_Flip_Flop d_ff_4 (.clk(clock_1_out), .D(and_6_out), .Q(b4));  // open: Qn, preset, en, reset
endmodule
