// Logisim project part1.circ as structural Verilog: 7 circuits, main circuit 4bitcounter
module _4bitcounter (
  input  CLK,
  input  INC,
  input  rst,
  output [3:0] OUT
);

  wire and_1_out, and_2_out, and_3_out, and_4_out, and_5_out, and_6_out, and_7_out, not_1_out, xor_1_out,
       xor_2_out, xor_3_out, xor_4_out;

  and and_1 (and_1_out, OUT[0], INC);
  and and_2 (and_2_out, and_1_out, OUT[1]);
  and and_3 (and_3_out, and_2_out, OUT[2]);
  xor xor_1 (xor_1_out, OUT[0], INC);
  xor xor_2 (xor_2_out, and_1_out, OUT[1]);
  xor xor_3 (xor_3_out, and_2_out, OUT[2]);
  xor xor_4 (xor_4_out, and_3_out, OUT[3]);
  and and_4 (and_4_out, xor_1_out, not_1_out);
  and and_5 (and_5_out, xor_2_out, not_1_out);
  and and_6 (and_6_out, xor_3_out, not_1_out);
  and and_7 (and_7_out, xor_4_out, not_1_out);
  not not_1 (not_1_out, rst);
  D_Flip_Flop d_ff_1 (.clk(CLK), .D(and_4_out), .Q(OUT[0]));  // open: Qn, preset, en, reset
  D_Flip_Flop d_ff_2 (.clk(CLK), .D(and_5_out), .Q(OUT[1]));  // open: Qn, preset, en, reset
  D_Flip_Flop d_ff_3 (.clk(CLK), .D(and_6_out), .Q(OUT[2]));  // open: Qn, preset, en, reset
  D_Flip_Flop d_ff_4 (.clk(CLK), .D(and_7_out), .Q(OUT[3]));  // open: Qn, preset, en, reset
endmodule

module _16_bit_register (
  input  [15:0] in_1,
  input  CLK,
  input  CLR,
  input  LOAD,
  input  INC,
  output [15:0] out_6
);

  wire and_1_out, and_2_out, and_3_out, and_4_out, and_5_out, and_6_out, and_7_out, and_8_out, and_9_out,
       and_10_out, and_11_out, and_12_out, and_13_out, and_14_out, and_15_out, and_16_out, and_17_out,
       and_18_out, and_19_out, and_20_out, and_21_out, and_22_out, and_23_out, and_24_out, and_25_out,
       and_26_out, and_27_out, and_28_out, and_29_out, and_30_out, and_31_out, and_32_out, and_33_out,
       and_34_out, and_35_out, and_36_out, inc_2_out, inc_3_out, inc_out, load0_2_out, load0_3_out,
       load0_4_out, load0_out, load1_2_out, load1_3_out, load1_4_out, load1_out, not_1_out, not_2_out,
       not_3_out, not_4_out, not_5_out, not_6_out, not_7_out, not_8_out, not_9_out, not_10_out, not_11_out,
       not_12_out, not_13_out, not_14_out, not_15_out, not_16_out, or_1_out, or_2_out, or_3_out, or_4_out,
       or_5_out, or_6_out, or_7_out, or_8_out, or_9_out, or_10_out, or_11_out, or_12_out, or_13_out,
       or_14_out, or_15_out, or_16_out, or_17_out, or_18_out, or_19_out, or_20_out, or_21_out, or_22_out,
       or_23_out, or_24_out, or_25_out, or_26_out, or_27_out, or_28_out, or_29_out, or_30_out, or_31_out,
       or_32_out;

  not not_1 (not_1_out, in_1[0]);
  not not_2 (not_2_out, in_1[1]);
  not not_3 (not_3_out, in_1[2]);
  not not_4 (not_4_out, in_1[3]);
  and load1 (load1_out, in_1[0], LOAD);
  and load0 (load0_out, not_1_out, LOAD);
  and load1_2 (load1_2_out, in_1[1], LOAD);
  and u_inc (inc_out, out_6[0], INC);
  and load0_2 (load0_2_out, not_2_out, LOAD);
  and load1_3 (load1_3_out, in_1[2], LOAD);
  and inc_2 (inc_2_out, inc_out, out_6[1]);
  and load0_3 (load0_3_out, not_3_out, LOAD);
  and load1_4 (load1_4_out, in_1[3], LOAD);
  and inc_3 (inc_3_out, inc_2_out, out_6[2]);
  and load0_4 (load0_4_out, not_4_out, LOAD);
  or or_1 (or_1_out, load1_out, INC);
  J_K_Flip_Flop b0 (.J(or_1_out), .clk(CLK), .K(or_2_out), .Q(out_6[0]));  // open: Qn, preset, en, reset
  or or_2 (or_2_out, INC, load0_out, CLR);
  or or_3 (or_3_out, load1_2_out, inc_out);
  J_K_Flip_Flop b1 (.J(or_3_out), .clk(CLK), .K(or_4_out), .Q(out_6[1]));  // open: Qn, preset, en, reset
  or or_4 (or_4_out, inc_out, load0_2_out, CLR);
  or or_5 (or_5_out, load1_3_out, inc_2_out);
  J_K_Flip_Flop b2 (.J(or_5_out), .clk(CLK), .K(or_6_out), .Q(out_6[2]));  // open: Qn, preset, en, reset
  or or_6 (or_6_out, inc_2_out, load0_3_out, CLR);
  or or_7 (or_7_out, load1_4_out, inc_3_out);
  J_K_Flip_Flop b3 (.J(or_7_out), .clk(CLK), .K(or_8_out), .Q(out_6[3]));  // open: Qn, preset, en, reset
  or or_8 (or_8_out, inc_3_out, load0_4_out, CLR);
  not not_5 (not_5_out, in_1[4]);
  not not_6 (not_6_out, in_1[5]);
  not not_7 (not_7_out, in_1[6]);
  not not_8 (not_8_out, in_1[7]);
  and and_1 (and_1_out, in_1[4], LOAD);
  and and_2 (and_2_out, inc_3_out, out_6[3]);
  and and_3 (and_3_out, not_5_out, LOAD);
  and and_4 (and_4_out, in_1[5], LOAD);
  and and_5 (and_5_out, and_2_out, out_6[4]);
  and and_6 (and_6_out, not_6_out, LOAD);
  and and_7 (and_7_out, in_1[6], LOAD);
  and and_8 (and_8_out, and_5_out, out_6[5]);
  and and_9 (and_9_out, not_7_out, LOAD);
  and and_10 (and_10_out, in_1[7], LOAD);
  and and_11 (and_11_out, and_8_out, out_6[6]);
  and and_12 (and_12_out, not_8_out, LOAD);
  or or_9 (or_9_out, and_1_out, and_2_out);
  or or_10 (or_10_out, and_2_out, and_3_out, CLR);
  or or_11 (or_11_out, and_4_out, and_5_out);
  or or_12 (or_12_out, and_5_out, and_6_out, CLR);
  or or_13 (or_13_out, and_7_out, and_8_out);
  or or_14 (or_14_out, and_8_out, and_9_out, CLR);
  or or_15 (or_15_out, and_10_out, and_11_out);
  or or_16 (or_16_out, and_11_out, and_12_out, CLR);
  J_K_Flip_Flop b4 (.J(or_9_out), .clk(CLK), .K(or_10_out), .Q(out_6[4]));  // open: Qn, preset, en, reset
  J_K_Flip_Flop b5 (.J(or_11_out), .clk(CLK), .K(or_12_out), .Q(out_6[5]));  // open: Qn, preset, en, reset
  J_K_Flip_Flop b6 (.J(or_13_out), .clk(CLK), .K(or_14_out), .Q(out_6[6]));  // open: Qn, preset, en, reset
  J_K_Flip_Flop b7 (.J(or_15_out), .clk(CLK), .K(or_16_out), .Q(out_6[7]));  // open: Qn, preset, en, reset
  not not_9 (not_9_out, in_1[8]);
  not not_10 (not_10_out, in_1[9]);
  not not_11 (not_11_out, in_1[10]);
  not not_12 (not_12_out, in_1[11]);
  and and_13 (and_13_out, in_1[8], LOAD);
  and and_14 (and_14_out, and_11_out, out_6[7]);
  and and_15 (and_15_out, not_9_out, LOAD);
  and and_16 (and_16_out, in_1[9], LOAD);
  and and_17 (and_17_out, and_14_out, out_6[8]);
  and and_18 (and_18_out, not_10_out, LOAD);
  and and_19 (and_19_out, in_1[10], LOAD);
  and and_20 (and_20_out, and_17_out, out_6[9]);
  and and_21 (and_21_out, not_11_out, LOAD);
  and and_22 (and_22_out, in_1[11], LOAD);
  and and_23 (and_23_out, and_20_out, out_6[10]);
  and and_24 (and_24_out, not_12_out, LOAD);
  or or_17 (or_17_out, and_13_out, and_14_out);
  or or_18 (or_18_out, and_14_out, and_15_out, CLR);
  or or_19 (or_19_out, and_16_out, and_17_out);
  or or_20 (or_20_out, and_17_out, and_18_out, CLR);
  or or_21 (or_21_out, and_19_out, and_20_out);
  or or_22 (or_22_out, and_20_out, and_21_out, CLR);
  or or_23 (or_23_out, and_22_out, and_23_out);
  or or_24 (or_24_out, and_23_out, and_24_out, CLR);
  J_K_Flip_Flop b4_2 (.J(or_17_out), .clk(CLK), .K(or_18_out), .Q(out_6[8]));  // open: Qn, preset, en, reset
  J_K_Flip_Flop b5_2 (.J(or_19_out), .clk(CLK), .K(or_20_out), .Q(out_6[9]));  // open: Qn, preset, en, reset
  J_K_Flip_Flop b6_2 (.J(or_21_out), .clk(CLK), .K(or_22_out), .Q(out_6[10]));  // open: Qn, preset, en, reset
  J_K_Flip_Flop b7_2 (.J(or_23_out), .clk(CLK), .K(or_24_out), .Q(out_6[11]));  // open: Qn, preset, en, reset
  not not_13 (not_13_out, in_1[12]);
  not not_14 (not_14_out, in_1[13]);
  not not_15 (not_15_out, in_1[14]);
  not not_16 (not_16_out, in_1[15]);
  and and_25 (and_25_out, in_1[12], LOAD);
  and and_26 (and_26_out, and_23_out, out_6[11]);
  and and_27 (and_27_out, not_13_out, LOAD);
  and and_28 (and_28_out, in_1[13], LOAD);
  and and_29 (and_29_out, and_26_out, out_6[12]);
  and and_30 (and_30_out, not_14_out, LOAD);
  and and_31 (and_31_out, in_1[14], LOAD);
  and and_32 (and_32_out, and_29_out, out_6[13]);
  and and_33 (and_33_out, not_15_out, LOAD);
  and and_34 (and_34_out, in_1[15], LOAD);
  and and_35 (and_35_out, and_32_out, out_6[14]);
  and and_36 (and_36_out, not_16_out, LOAD);
  or or_25 (or_25_out, and_25_out, and_26_out);
  or or_26 (or_26_out, and_26_out, and_27_out, CLR);
  or or_27 (or_27_out, and_28_out, and_29_out);
  or or_28 (or_28_out, and_29_out, and_30_out, CLR);
  or or_29 (or_29_out, and_31_out, and_32_out);
  or or_30 (or_30_out, and_32_out, and_33_out, CLR);
  or or_31 (or_31_out, and_34_out, and_35_out);
  or or_32 (or_32_out, and_35_out, and_36_out, CLR);
  J_K_Flip_Flop b4_3 (.J(or_25_out), .clk(CLK), .K(or_26_out), .Q(out_6[12]));  // open: Qn, preset, en, reset
  J_K_Flip_Flop b5_3 (.J(or_27_out), .clk(CLK), .K(or_28_out), .Q(out_6[13]));  // open: Qn, preset, en, reset
  J_K_Flip_Flop b6_3 (.J(or_29_out), .clk(CLK), .K(or_30_out), .Q(out_6[14]));  // open: Qn, preset, en, reset
  J_K_Flip_Flop b7_3 (.J(or_31_out), .clk(CLK), .K(or_32_out), .Q(out_6[15]));  // open: Qn, preset, en, reset
endmodule

module RegisterDemo (
  output [3:0] out_1,
  output [15:0] out_2,
  output [15:0] out_3
);

  wire clock_1_out, multiplexer_1_out, multiplexer_2_out;

  Clock clock_1 (.out(clock_1_out));
  _4bitcounter SC (.CLK(clock_1_out), .INC(1'b1), .rst(multiplexer_2_out), .OUT(out_1));
  Multiplexer #(.select(4)) multiplexer_1 (
    .in0(1'b1), .in1(1'b0), .in2(1'b0), .in3(1'b0), .in4(1'b0), .in5(1'b0), .in6(1'b0), .in7(1'b0),
    .in8(1'b0), .in9(1'b0), .in10(1'b0), .in11(1'b0), .in12(1'b0), .in13(1'b0), .in14(1'b0), .in15(1'b0),
    .out(multiplexer_1_out), .sel(out_1));  // open: en
  _16_bit_register PC (
    .in_1({16{1'b0}}), .CLK(clock_1_out), .LOAD(1'b0), .INC(multiplexer_1_out), .CLR(1'b0), .out_6(out_2));
  _16_bit_register AR (
    .in_1(out_2), .CLK(clock_1_out), .LOAD(multiplexer_1_out), .INC(1'b0), .CLR(multiplexer_2_out),
    .out_6(out_3));
  Multiplexer #(.select(4)) multiplexer_2 (
    .in0(1'b0), .in1(1'b1), .in2(1'b0), .in3(1'b0), .in4(1'b0), .in5(1'b0), .in6(1'b0), .in7(1'b0),
    .in8(1'b0), .in9(1'b0), .in10(1'b0), .in11(1'b0), .in12(1'b0), .in13(1'b0), .in14(1'b0), .in15(1'b0),
    .out(multiplexer_2_out), .sel(out_1));  // open: en

  // Notes on the sheet:
  //   t0
  //   t1
endmodule

module Adder (
  output [3:0] \output 
);

  wire and_1_out, and_2_out, and_3_out, and_4_out, and_5_out, and_6_out, and_7_out, and_8_out, and_9_out,
       and_10_out, and_11_out, button_1_out, clock_1_out, not_1_out, xor_1_out, xor_2_out, xor_3_out,
       xor_4_out;

  Clock clock_1 (.out(clock_1_out));
  xor xor_1 (xor_1_out, 1'b1, \output [0]);
  and and_1 (and_1_out, \output [0], 1'b1);
  and and_2 (and_2_out, \output [1], and_5_out);
  and and_3 (and_3_out, \output [2], and_6_out);
  and and_4 (and_4_out, \output [3], and_7_out);
  LED led_1 (.in(and_4_out));
  xor xor_2 (xor_2_out, and_1_out, \output [1]);
  and and_5 (and_5_out, \output [1], and_1_out);
  xor xor_3 (xor_3_out, and_2_out, \output [2]);
  and and_6 (and_6_out, \output [2], and_2_out);
  xor xor_4 (xor_4_out, and_3_out, \output [3]);
  and and_7 (and_7_out, \output [3], and_3_out);
  not not_1 (not_1_out, button_1_out);
  Button button_1 (.out(button_1_out));
  and and_8 (and_8_out, xor_1_out, not_1_out);
  and and_9 (and_9_out, xor_2_out, not_1_out);
  and and_10 (and_10_out, xor_3_out, not_1_out);
  and and_11 (and_11_out, xor_4_out, not_1_out);
  D_Flip_Flop d_ff_1 (.clk(clock_1_out), .D(and_8_out), .Q(\output [0]));  // open: Qn, preset, en, reset
  D_Flip_Flop d_ff_2 (.clk(clock_1_out), .D(and_9_out), .Q(\output [1]));  // open: Qn, preset, en, reset
  D_Flip_Flop d_ff_3 (.clk(clock_1_out), .D(and_10_out), .Q(\output [2]));  // open: Qn, preset, en, reset
  D_Flip_Flop d_ff_4 (.clk(clock_1_out), .D(and_11_out), .Q(\output [3]));  // open: Qn, preset, en, reset

  // Other names for the same wires on the sheet: B1 = \output [0]; B2 = \output [1]; B3 = \output [2];
  //   B4 = \output [3]
endmodule

module RAMDemo (
  output [3:0] out_1,
  output [15:0] out_2,
  output [15:0] out_3,
  output [15:0] out_4,
  output [15:0] out_5
);

  wire clock_1_out, multiplexer_1_out, multiplexer_2_out, multiplexer_3_out;

  Clock clock_1 (.out(clock_1_out));
  _4bitcounter SC (.CLK(clock_1_out), .INC(1'b1), .rst(multiplexer_3_out), .OUT(out_1));
  Multiplexer #(.select(4)) multiplexer_1 (
    .in0(1'b1), .in1(1'b0), .in2(1'b0), .in3(1'b0), .in4(1'b0), .in5(1'b0), .in6(1'b0), .in7(1'b0),
    .in8(1'b0), .in9(1'b0), .in10(1'b0), .in11(1'b0), .in12(1'b0), .in13(1'b0), .in14(1'b0), .in15(1'b0),
    .out(multiplexer_1_out), .sel(out_1));  // open: en
  _16_bit_register PC (
    .in_1({16{1'b0}}), .CLK(clock_1_out), .LOAD(1'b0), .INC(multiplexer_1_out), .CLR(1'b0), .out_6(out_2));
  _16_bit_register AR (
    .in_1(out_2), .CLK(clock_1_out), .LOAD(multiplexer_1_out), .INC(1'b0), .CLR(1'b0), .out_6(out_3));
  Multiplexer #(.select(4)) multiplexer_2 (
    .in0(1'b0), .in1(1'b1), .in2(1'b0), .in3(1'b0), .in4(1'b0), .in5(1'b0), .in6(1'b0), .in7(1'b0),
    .in8(1'b0), .in9(1'b0), .in10(1'b0), .in11(1'b0), .in12(1'b0), .in13(1'b0), .in14(1'b0), .in15(1'b0),
    .out(multiplexer_2_out), .sel(out_1));  // open: en
  _16_bit_register IR (
    .in_1(out_4), .CLK(clock_1_out), .LOAD(multiplexer_2_out), .INC(1'b0), .CLR(1'b0), .out_6(out_5));
  Multiplexer #(.select(4)) multiplexer_3 (
    .in0(1'b0), .in1(1'b0), .in2(1'b1), .in3(1'b0), .in4(1'b0), .in5(1'b0), .in6(1'b0), .in7(1'b0),
    .in8(1'b0), .in9(1'b0), .in10(1'b0), .in11(1'b0), .in12(1'b0), .in13(1'b0), .in14(1'b0), .in15(1'b0),
    .out(multiplexer_3_out), .sel(out_1));  // open: en
  RAM #(.addrWidth(12), .dataWidth(16), .bus("separate")) ram_1 (
    .addr(out_3[11:0]), .data(out_4), .clk(clock_1_out), .ld(1'b1));  // open: din, str, sel, clr

  // Notes on the sheet:
  //   t0
  //   t1
  //   t2
endmodule

module _16_bit_register_copy (
  input  [15:0] in_1,
  input  CLK,
  input  LOAD,
  input  INC,
  input  CLR,
  output [15:0] out_6
);

  wire and_1_out, and_2_out, and_3_out, and_4_out, and_5_out, and_6_out, and_7_out, and_8_out, and_9_out,
       and_10_out, and_11_out, and_12_out, and_13_out, and_14_out, and_15_out, and_16_out, and_17_out,
       and_18_out, and_19_out, and_20_out, and_21_out, and_22_out, and_23_out, and_24_out, and_25_out,
       and_26_out, and_27_out, and_28_out, and_29_out, and_30_out, and_31_out, or_1_out, or_2_out, or_3_out,
       or_4_out, or_5_out, or_6_out, or_7_out, or_8_out, or_9_out, or_10_out, or_11_out, or_12_out,
       or_13_out, or_14_out, or_15_out, or_16_out, or_17_out, or_18_out, or_19_out, or_20_out, or_21_out,
       or_22_out, or_23_out, or_24_out, or_25_out, or_26_out, or_27_out, or_28_out, or_29_out, or_30_out,
       or_31_out, or_32_out, xor_1_out, xor_2_out, xor_3_out, xor_4_out, xor_5_out, xor_6_out, xor_7_out,
       xor_8_out, xor_9_out, xor_10_out, xor_11_out, xor_12_out, xor_13_out, xor_14_out, xor_15_out,
       xor_16_out;

  xor xor_1 (xor_1_out, in_1[0], out_6[0]);
  xor xor_2 (xor_2_out, in_1[1], out_6[1]);
  xor xor_3 (xor_3_out, in_1[2], out_6[2]);
  xor xor_4 (xor_4_out, in_1[3], out_6[3]);
  and and_1 (and_1_out, xor_1_out, LOAD);
  and and_2 (and_2_out, xor_2_out, LOAD);
  and and_3 (and_3_out, out_6[0], INC);
  and and_4 (and_4_out, xor_3_out, LOAD);
  and and_5 (and_5_out, and_3_out, out_6[1]);
  and and_6 (and_6_out, xor_4_out, LOAD);
  and and_7 (and_7_out, and_5_out, out_6[2]);
  or or_1 (or_1_out, and_1_out, INC);
  J_K_Flip_Flop b0 (.J(or_1_out), .clk(CLK), .K(or_2_out), .Q(out_6[0]));  // open: Qn, preset, en, reset
  or or_2 (or_2_out, INC, CLR);
  or or_3 (or_3_out, and_2_out, and_3_out);
  J_K_Flip_Flop b1 (.J(or_3_out), .clk(CLK), .K(or_4_out), .Q(out_6[1]));  // open: Qn, preset, en, reset
  or or_4 (or_4_out, and_3_out, CLR);
  or or_5 (or_5_out, and_4_out, and_5_out);
  J_K_Flip_Flop b2 (.J(or_5_out), .clk(CLK), .K(or_6_out), .Q(out_6[2]));  // open: Qn, preset, en, reset
  or or_6 (or_6_out, and_5_out, CLR);
  or or_7 (or_7_out, and_6_out, and_7_out);
  J_K_Flip_Flop b3 (.J(or_7_out), .clk(CLK), .K(or_8_out), .Q(out_6[3]));  // open: Qn, preset, en, reset
  or or_8 (or_8_out, and_7_out, CLR);
  xor xor_5 (xor_5_out, in_1[4], out_6[4]);
  xor xor_6 (xor_6_out, in_1[5], out_6[5]);
  xor xor_7 (xor_7_out, in_1[6], out_6[6]);
  xor xor_8 (xor_8_out, in_1[7], out_6[7]);
  and and_8 (and_8_out, xor_5_out, LOAD);
  and and_9 (and_9_out, and_7_out, out_6[3]);
  and and_10 (and_10_out, xor_6_out, LOAD);
  and and_11 (and_11_out, and_9_out, out_6[4]);
  and and_12 (and_12_out, xor_7_out, LOAD);
  and and_13 (and_13_out, and_11_out, out_6[5]);
  and and_14 (and_14_out, xor_8_out, LOAD);
  and and_15 (and_15_out, and_13_out, out_6[6]);
  or or_9 (or_9_out, and_8_out, and_9_out);
  or or_10 (or_10_out, and_9_out, CLR);
  or or_11 (or_11_out, and_10_out, and_11_out);
  or or_12 (or_12_out, and_11_out, CLR);
  or or_13 (or_13_out, and_12_out, and_13_out);
  or or_14 (or_14_out, and_13_out, CLR);
  or or_15 (or_15_out, and_14_out, and_15_out);
  or or_16 (or_16_out, and_15_out, CLR);
  J_K_Flip_Flop b4 (.J(or_9_out), .clk(CLK), .K(or_10_out), .Q(out_6[4]));  // open: Qn, preset, en, reset
  J_K_Flip_Flop b5 (.J(or_11_out), .clk(CLK), .K(or_12_out), .Q(out_6[5]));  // open: Qn, preset, en, reset
  J_K_Flip_Flop b6 (.J(or_13_out), .clk(CLK), .K(or_14_out), .Q(out_6[6]));  // open: Qn, preset, en, reset
  J_K_Flip_Flop b7 (.J(or_15_out), .clk(CLK), .K(or_16_out), .Q(out_6[7]));  // open: Qn, preset, en, reset
  xor xor_9 (xor_9_out, in_1[8], out_6[8]);
  xor xor_10 (xor_10_out, in_1[9], out_6[9]);
  xor xor_11 (xor_11_out, in_1[10], out_6[10]);
  xor xor_12 (xor_12_out, in_1[11], out_6[11]);
  and and_16 (and_16_out, xor_9_out, LOAD);
  and and_17 (and_17_out, and_15_out, out_6[7]);
  and and_18 (and_18_out, xor_10_out, LOAD);
  and and_19 (and_19_out, and_17_out, out_6[8]);
  and and_20 (and_20_out, xor_11_out, LOAD);
  and and_21 (and_21_out, and_19_out, out_6[9]);
  and and_22 (and_22_out, xor_12_out, LOAD);
  and and_23 (and_23_out, and_21_out, out_6[10]);
  or or_17 (or_17_out, and_16_out, and_17_out);
  or or_18 (or_18_out, and_17_out, CLR);
  or or_19 (or_19_out, and_18_out, and_19_out);
  or or_20 (or_20_out, and_19_out, CLR);
  or or_21 (or_21_out, and_20_out, and_21_out);
  or or_22 (or_22_out, and_21_out, CLR);
  or or_23 (or_23_out, and_22_out, and_23_out);
  or or_24 (or_24_out, and_23_out, CLR);
  J_K_Flip_Flop b4_2 (.J(or_17_out), .clk(CLK), .K(or_18_out), .Q(out_6[8]));  // open: Qn, preset, en, reset
  J_K_Flip_Flop b5_2 (.J(or_19_out), .clk(CLK), .K(or_20_out), .Q(out_6[9]));  // open: Qn, preset, en, reset
  J_K_Flip_Flop b6_2 (.J(or_21_out), .clk(CLK), .K(or_22_out), .Q(out_6[10]));  // open: Qn, preset, en, reset
  J_K_Flip_Flop b7_2 (.J(or_23_out), .clk(CLK), .K(or_24_out), .Q(out_6[11]));  // open: Qn, preset, en, reset
  xor xor_13 (xor_13_out, in_1[12], out_6[12]);
  xor xor_14 (xor_14_out, in_1[13], out_6[13]);
  xor xor_15 (xor_15_out, in_1[14], out_6[14]);
  xor xor_16 (xor_16_out, in_1[15], out_6[15]);
  and and_24 (and_24_out, xor_13_out, LOAD);
  and and_25 (and_25_out, and_23_out, out_6[11]);
  and and_26 (and_26_out, xor_14_out, LOAD);
  and and_27 (and_27_out, and_25_out, out_6[12]);
  and and_28 (and_28_out, xor_15_out, LOAD);
  and and_29 (and_29_out, and_27_out, out_6[13]);
  and and_30 (and_30_out, xor_16_out, LOAD);
  and and_31 (and_31_out, and_29_out, out_6[14]);
  or or_25 (or_25_out, and_24_out, and_25_out);
  or or_26 (or_26_out, and_25_out, CLR);
  or or_27 (or_27_out, and_26_out, and_27_out);
  or or_28 (or_28_out, and_27_out, CLR);
  or or_29 (or_29_out, and_28_out, and_29_out);
  or or_30 (or_30_out, and_29_out, CLR);
  or or_31 (or_31_out, and_30_out, and_31_out);
  or or_32 (or_32_out, and_31_out, CLR);
  J_K_Flip_Flop b4_3 (.J(or_25_out), .clk(CLK), .K(or_26_out), .Q(out_6[12]));  // open: Qn, preset, en, reset
  J_K_Flip_Flop b5_3 (.J(or_27_out), .clk(CLK), .K(or_28_out), .Q(out_6[13]));  // open: Qn, preset, en, reset
  J_K_Flip_Flop b6_3 (.J(or_29_out), .clk(CLK), .K(or_30_out), .Q(out_6[14]));  // open: Qn, preset, en, reset
  J_K_Flip_Flop b7_3 (.J(or_31_out), .clk(CLK), .K(or_32_out), .Q(out_6[15]));  // open: Qn, preset, en, reset
endmodule

module RegisterDemo_copy (
  output [3:0] out_1,
  output [15:0] out_2,
  output [15:0] out_3
);

  wire clock_1_out, multiplexer_1_out, multiplexer_2_out;

  Clock clock_1 (.out(clock_1_out));
  _4bitcounter SC (.CLK(clock_1_out), .INC(1'b1), .rst(multiplexer_2_out), .OUT(out_1));
  Multiplexer #(.select(4)) multiplexer_1 (
    .in0(1'b1), .in1(1'b0), .in2(1'b0), .in3(1'b0), .in4(1'b0), .in5(1'b0), .in6(1'b0), .in7(1'b0),
    .in8(1'b0), .in9(1'b0), .in10(1'b0), .in11(1'b0), .in12(1'b0), .in13(1'b0), .in14(1'b0), .in15(1'b0),
    .out(multiplexer_1_out), .sel(out_1));  // open: en
  _16_bit_register_copy PC (
    .in_1({16{1'b0}}), .CLK(clock_1_out), .LOAD(1'b0), .INC(multiplexer_1_out), .CLR(1'b0), .out_6(out_2));
  _16_bit_register_copy AR (
    .in_1(out_2), .CLK(clock_1_out), .LOAD(multiplexer_1_out), .INC(1'b0), .CLR(multiplexer_2_out),
    .out_6(out_3));
  Multiplexer #(.select(4)) multiplexer_2 (
    .in0(1'b0), .in1(1'b1), .in2(1'b0), .in3(1'b0), .in4(1'b0), .in5(1'b0), .in6(1'b0), .in7(1'b0),
    .in8(1'b0), .in9(1'b0), .in10(1'b0), .in11(1'b0), .in12(1'b0), .in13(1'b0), .in14(1'b0), .in15(1'b0),
    .out(multiplexer_2_out), .sel(out_1));  // open: en

  // Notes on the sheet:
  //   t0
  //   t1
endmodule
